// Logisim project control-logic.circ as structural Verilog: 1 circuit, main circuit control_logic
module control_logic (
  input  [31:0] Instruction,
  input  BrEq,
  input  BrLt,
  output PCSel,
  output RegWEn,
  output [2:0] ImmSel,
  output BrUn,
  output ASel,
  output BSel,
  output [3:0] ALUSel,
  output MemRW,
  output [1:0] WBSel
);

  wire is_add, is_and, is_mul, is_mulh, is_mulhu, is_or, is_sll, is_slt, is_sra, is_srl, is_sub, is_xor;
  wire [5:0] priority_encoder_1_out;
  wire [15:14] rom_1_data;

  Comparator #(.width(17)) comparator_1 (
    .a({Instruction[31:25], Instruction[14:12], Instruction[6:0]}), .b(17'h433), .eq(is_and));  // open: gt, lt
  Comparator #(.width(17)) comparator_2 (
    .a({Instruction[31:25], Instruction[14:12], Instruction[6:0]}), .b(17'h33), .eq(is_add));  // open: gt, lt
  Comparator #(.width(17)) comparator_3 (
    .a({Instruction[31:25], Instruction[14:12], Instruction[6:0]}), .b(17'h433), .eq(is_mul));  // open: gt, lt
  Comparator #(.width(17)) comparator_4 (
    .a({Instruction[31:25], Instruction[14:12], Instruction[6:0]}), .b(17'h8033), .eq(is_sub));  // open: gt, lt
  Comparator #(.width(17)) comparator_5 (
    .a({Instruction[31:25], Instruction[14:12], Instruction[6:0]}), .b(17'h433), .eq(is_sll));  // open: gt, lt
  Comparator #(.width(17)) comparator_6 (
    .a({Instruction[31:25], Instruction[14:12], Instruction[6:0]}), .b(17'h433), .eq(is_mulh));  // open: gt, lt
  Comparator #(.width(17)) comparator_7 (
    .a({Instruction[31:25], Instruction[14:12], Instruction[6:0]}), .b(17'h433), .eq(is_mulhu));  // open: gt, lt
  Comparator #(.width(17)) comparator_8 (
    .a({Instruction[31:25], Instruction[14:12], Instruction[6:0]}), .b(17'h433), .eq(is_slt));  // open: gt, lt
  Comparator #(.width(17)) comparator_9 (
    .a({Instruction[31:25], Instruction[14:12], Instruction[6:0]}), .b(17'h433), .eq(is_xor));  // open: gt, lt
  Comparator #(.width(17)) comparator_10 (
    .a({Instruction[31:25], Instruction[14:12], Instruction[6:0]}), .b(17'h433), .eq(is_srl));  // open: gt, lt
  Comparator #(.width(17)) comparator_11 (
    .a({Instruction[31:25], Instruction[14:12], Instruction[6:0]}), .b(17'h433), .eq(is_sra));  // open: gt, lt
  Comparator #(.width(17)) comparator_12 (
    .a({Instruction[31:25], Instruction[14:12], Instruction[6:0]}), .b(17'h433), .eq(is_or));  // open: gt, lt
  ROM #(.addrWidth(6), .dataWidth(16)) rom_1 (.data({rom_1_data, WBSel, MemRW, ALUSel, BSel, ASel, BrUn, ImmSel, RegWEn}));  // open: addr
  Priority_Encoder #(.select_enc(6)) priority_encoder_1 (
    .in0(is_add), .out(priority_encoder_1_out));  // open: in1, in2, in3, in4, in5, in6, in7, in8, in9, in10, in11, in12, in13, in14, in15, in16, in17, in18, in19, in20, in21, in22, in23, in24, in25, in26, in27, in28, in29, in30, in31, in32, in33, in34, in35, in36, in37, in38, in39, in40, in41, in42, in43, in44, in45, in46, in47, in48, in49, in50, in51, in52, in53, in54, in55, in56, in57, in58, in59, in60, in61, in62, in63, gs, en_out, en_in
  // Probe on priority_encoder_1_out

  // Other names for the same wires on the sheet: Opcode[6:0] = Instruction[6:0]; Funct3[2:0] = Instruction[14:12];
  //   Funct7[6:0] = Instruction[31:25]

  // Notes on the sheet:
  //   INPUTS to your circuit
  //   Connect ROM Input here ->
  //   contents of rom_1 (hex, n*v repeats v):
  //   1001 1401 1601 1081 1481 1581 1101 1201 1281 1681 1301 1381 41 41 41 1041 10c1 1141 1241 12c1 16c1
  //   1341 13c1 842 842 842 4*64 74 74 1067 17c7 2069 2041
  //   ROM FOR CONTROL LOGIC
  //   DON'T CHANGE THE LOCATIONS OF THE INPUTS AND OUTPUTS!
  //   This is only if you choose to do the ROM option
  //   OUTPUT from your circuit
  //   Reminder: If using ROM, use combinational logic for PCSel
  //   CONNECT
  //   WIRE
  //   TO
  //   USE
  //   ROM
endmodule
