// Logisim project cpu.circ as structural Verilog: 1 circuit, main circuit cpu
module cpu (
  input  clk,
  input  [31:0] Instruction,
  input  [31:0] MemReadData,
  output [31:0] MemAddress,
  output [31:0] ProgramCounter,
  output [31:0] ra,
  output [31:0] sp,
  output [31:0] t0,
  output [31:0] t1,
  output [31:0] t2,
  output [31:0] s0,
  output [31:0] s1,
  output [31:0] a0,
  output [3:0] MemWriteMask,
  output [31:0] MemWriteData
);

  wire ASel, BrEq, BrLt, BrUn, BSel, MemRW, partial_store_1_p4, partial_store_1_p5, partial_store_1_p7,
       partial_store_1_p9, PCSel, regfile_1_p7, regfile_1_p8, regfile_1_p10, regfile_1_p22, regfile_1_p24,
       RegWEn;
  wire [2:0] ImmSel;
  wire [3:0] ALUSel;
  wire [31:0] adder_1_out, ALUResult, Imm, multiplexer_1_out, multiplexer_2_out, multiplexer_3_out,
       regfile_1_p19, regfile_1_p20;

  Adder #(.width(32)) adder_1 (.a(ProgramCounter), .b(32'h4), .out(adder_1_out));  // open: cin, cout
  Register #(.width(32)) PC (.D(multiplexer_1_out), .clk(clk), .Q(ProgramCounter));  // open: en, clr
  Multiplexer #(.width(32)) multiplexer_1 (.in0(adder_1_out), .in1(ALUResult), .out(multiplexer_1_out), .sel(PCSel));
  imm_gen imm_gen_1 (.Instruction(Instruction), .ImmSel(ImmSel), .Immediate(Imm));
  control_logic control_logic_1 (
    .Instruction(Instruction), .BrEq(BrEq), .BrLt(BrLt), .PCSel(PCSel), .RegWEn(RegWEn), .ImmSel(ImmSel),
    .BrUn(BrUn), .ASel(ASel), .BSel(BSel), .ALUSel(ALUSel), .MemRW(MemRW));  // open: WBSel
  // regfile regfile_1: pin names not known; wires that end beside it: Instruction[19:15], Instruction[24:20], Instruction[11:7], ALUResult, RegWEn, clk, regfile_1_p7, regfile_1_p8, regfile_1_p8, regfile_1_p10, ra, sp, t0, t1, t2, s0, s1, a0, regfile_1_p19, regfile_1_p20, regfile_1_p10, regfile_1_p22, regfile_1_p22, regfile_1_p24, regfile_1_p24
  Multiplexer #(.width(32)) multiplexer_2 (
    .in0(regfile_1_p19), .in1(ProgramCounter), .out(multiplexer_2_out), .sel(ASel));
  Multiplexer #(.width(32)) multiplexer_3 (.in0(regfile_1_p20), .in1(Imm), .out(multiplexer_3_out), .sel(BSel));
  // branch_comp branch_comp_1: pin names not known; wires that end beside it: regfile_1_p19, regfile_1_p20, BrUn, BrEq, BrLt
  alu alu_1 (.A(multiplexer_2_out), .B(multiplexer_3_out), .ALUSel(ALUSel), .ALUResult(ALUResult));
  // partial_store partial_store_1: pin names not known; wires that end beside it: Instruction, MemAddress, MemRW, partial_store_1_p4, partial_store_1_p5, partial_store_1_p5, partial_store_1_p7, partial_store_1_p7, partial_store_1_p9, MemWriteMask, MemWriteData, partial_store_1_p4, partial_store_1_p9
  // partial_load partial_load_1: pin names not known; wires that end beside it: Instruction, MemAddress, MemReadData

  // Notes on the sheet:
  //   To IMEM
  //   IMEM (do **NOT** move this)
  //   From IMEM
  //   Inputs/Outputs for testing. Do **NOT** move these.
  //   To DMEM
  //   DMEM (do **NOT** move this)
  //   From DMEM
endmodule
